// Logisim project G38_th5_control.circ as structural Verilog: 37 circuits, main circuit tara_cpu
module main (
);

  tara_decoder tara_decoder_1 ();  // open: IR, off5, rel8, RB, imm8, rel11, RA, RD, op, format

  // Notes on the sheet:
  //   Group 38 | Roll number: CS25B035
endmodule

module tara_decoder (
  input  [15:0] IR,
  output [4:0] off5,
  output [7:0] rel8,
  output [2:0] RB,
  output [7:0] imm8,
  output [10:0] rel11,
  output [2:0] RA,
  output [2:0] RD,
  output [4:0] op,
  output [2:0] format
);

  op_to_format op_to_format_1 (.op(IR[15:11]), .F(format));

  assign imm8 = IR[7:0];
  assign off5 = IR[4:0];
  assign op = IR[15:11];
  assign RA = IR[7:5];
  assign RB = IR[4:2];
  assign RD = IR[10:8];
  assign rel8 = IR[7:0];
  assign rel11 = IR[10:0];

  // Notes on the sheet:
  //   Group 38 | Roll number: CS25B035
endmodule

module op_to_format (
  input  [4:0] op,
  output [2:0] F
);

  wire and_1_out, and_2_out, and_3_out, and_4_out, and_5_out, and_6_out, and_7_out, and_8_out, and_9_out,
       and_10_out, and_11_out, and_12_out, and_13_out, and_14_out, and_15_out, and_16_out, and_17_out,
       and_18_out, and_19_out, not_1_out, not_2_out, not_3_out, not_4_out, not_5_out;

  not not_1 (not_1_out, op[4]);
  not not_2 (not_2_out, op[3]);
  not not_3 (not_3_out, op[2]);
  not not_4 (not_4_out, op[1]);
  not not_5 (not_5_out, op[0]);
  and and_1 (and_1_out, op[4], op[2]);
  and and_2 (and_2_out, not_2_out, op[2], op[0]);
  and and_3 (and_3_out, not_2_out, op[2], op[1]);
  and and_4 (and_4_out, not_1_out, op[3], not_3_out, not_4_out, not_5_out);
  and and_5 (and_5_out, op[4], op[3], op[0]);
  and and_6 (and_6_out, op[4], op[3], op[1]);
  and and_7 (and_7_out, not_1_out, not_2_out, op[2], not_4_out, not_5_out);
  and and_8 (and_8_out, op[4], op[2], op[1]);
  and and_9 (and_9_out, op[4], not_3_out, not_4_out, op[0]);
  and and_10 (and_10_out, op[4], op[1], not_5_out);
  and and_11 (and_11_out, not_1_out, not_3_out, op[1], op[0]);
  and and_12 (and_12_out, op[4], not_2_out, not_3_out, not_4_out);
  and and_13 (and_13_out, not_1_out, not_2_out, not_3_out, op[1]);
  and and_14 (and_14_out, not_3_out, op[1], op[0]);
  and and_15 (and_15_out, op[2], not_4_out, not_5_out);
  and and_16 (and_16_out, op[3], op[0]);
  and and_17 (and_17_out, op[3], op[1]);
  and and_18 (and_18_out, op[4], not_3_out, op[1]);
  and and_19 (and_19_out, op[4], not_4_out, op[0]);
  or or_1 (F[2], and_1_out, and_2_out, and_3_out, and_4_out, and_5_out, and_6_out);
  or or_2 (F[1], and_7_out, and_8_out, and_9_out, and_10_out, and_11_out, and_12_out, and_13_out);
  or or_3 (F[0], and_14_out, and_15_out, and_16_out, and_17_out, and_18_out, and_19_out);

  // Notes on the sheet:
  //   Group 38 | Roll number: CS25B035
endmodule

module halfadder (
  input  A,
  input  B,
  output SUM,
  output Cout
);

  xor xor_1 (SUM, A, B);
  and and_1 (Cout, A, B);

  // Notes on the sheet:
  //   Group 38 | Roll number: CS25B035
endmodule

module fulladder (
  input  A,
  input  B,
  input  CIN,
  output SUM,
  output COUT
);

  wire and_1_out, and_2_out, xor_1_out;

  xor xor_1 (xor_1_out, A, B);
  and and_1 (and_1_out, A, B);
  or or_1 (COUT, and_1_out, and_2_out);
  xor xor_2 (SUM, xor_1_out, CIN);
  and and_2 (and_2_out, xor_1_out, CIN);

  // Notes on the sheet:
  //   Group 38 | Roll number: CS25B035
endmodule

module adder4 (
  input  CIN,
  input  [3:0] A,
  input  [3:0] B,
  output [3:0] SUM,
  output COUT,
  output cin_last
);

  wire fulladder_1_cout, fulladder_2_cout;

  fulladder fulladder_1 (.A(A[0]), .B(B[0]), .CIN(CIN), .SUM(SUM[0]), .COUT(fulladder_1_cout));
  fulladder fulladder_2 (.A(A[1]), .B(B[1]), .CIN(fulladder_1_cout), .SUM(SUM[1]), .COUT(fulladder_2_cout));
  fulladder fulladder_3 (.A(A[2]), .B(B[2]), .CIN(fulladder_2_cout), .SUM(SUM[2]), .COUT(cin_last));
  fulladder fulladder_4 (.A(A[3]), .B(B[3]), .CIN(cin_last), .SUM(SUM[3]), .COUT(COUT));

  // Notes on the sheet:
  //   Group 38 | Roll number: CS25B035
endmodule

module adder16 (
  input  CIN,
  input  [15:0] A,
  input  [15:0] B,
  output [15:0] SUM,
  output COUT,
  output cin_last
);

  wire adder4_1_cout, adder4_2_cout, adder4_3_cout;

  adder4 adder4_1 (.CIN(CIN), .A(A[3:0]), .B(B[3:0]), .SUM(SUM[3:0]), .COUT(adder4_1_cout));  // open: cin_last
  adder4 adder4_2 (
    .CIN(adder4_1_cout), .A(A[7:4]), .B(B[7:4]), .SUM(SUM[7:4]), .COUT(adder4_2_cout));  // open: cin_last
  adder4 adder4_3 (
    .CIN(adder4_2_cout), .A(A[11:8]), .B(B[11:8]), .SUM(SUM[11:8]), .COUT(adder4_3_cout));  // open: cin_last
  adder4 adder4_4 (.CIN(adder4_3_cout), .A(A[15:12]), .B(B[15:12]), .SUM(SUM[15:12]), .COUT(COUT), .cin_last(cin_last));

  // Notes on the sheet:
  //   Group 38 | Roll number: CS25B035
endmodule

module addsub16 (
  input  [15:0] A,
  input  [15:0] B,
  input  SUB,
  output [15:0] SUM,
  output OVF,
  output COUT
);

  wire adder16_1_cin_last;
  wire [15:0] multiplexer_1_out, not_1_out;

  Multiplexer #(.width(16)) multiplexer_1 (.in0(B), .in1(not_1_out), .out(multiplexer_1_out), .sel(SUB));
  assign not_1_out = ~B;  // NOT_Gate not_1, 16 bits wide
  adder16 adder16_1 (.CIN(SUB), .A(A), .B(multiplexer_1_out), .SUM(SUM), .COUT(COUT), .cin_last(adder16_1_cin_last));
  xor xor_1 (OVF, COUT, adder16_1_cin_last);

  // Notes on the sheet:
  //   Group 38 | Roll number: CS25B035
endmodule

module cmp1 (
  input  LTin,
  input  A,
  input  B,
  input  EQin,
  input  GTin,
  output LT,
  output GT,
  output EQ
);

  wire and_1_out, and_2_out, and_3_out, and_4_out, not_1_out, not_2_out, xnor_1_out;

  not not_1 (not_1_out, A);
  not not_2 (not_2_out, B);
  and and_1 (and_1_out, not_1_out, B);
  and and_2 (and_2_out, A, not_2_out);
  xnor xnor_1 (xnor_1_out, B, A);
  and and_3 (and_3_out, and_1_out, EQin);
  and and_4 (and_4_out, EQin, and_2_out);
  and and_5 (EQ, EQin, xnor_1_out);
  or or_1 (LT, LTin, and_3_out);
  or or_2 (GT, GTin, and_4_out);

  // Notes on the sheet:
  //   ~AB
  //   A~B
  //   Group 38 | Roll number: CS25B035
endmodule

module cmp4 (
  input  LTin,
  input  EQin,
  input  GTin,
  input  [3:0] A,
  input  [3:0] B,
  output LT,
  output GT,
  output EQ
);

  wire cmp1_1_eq, cmp1_1_gt, cmp1_1_lt, cmp1_2_eq, cmp1_2_gt, cmp1_2_lt, cmp1_3_eq, cmp1_3_gt, cmp1_3_lt;

  cmp1 cmp1_1 (
    .LTin(LTin), .A(A[3]), .B(B[3]), .EQin(EQin), .GTin(GTin), .LT(cmp1_1_lt), .GT(cmp1_1_gt), .EQ(cmp1_1_eq));
  cmp1 cmp1_2 (
    .LTin(cmp1_1_lt), .A(A[2]), .B(B[2]), .EQin(cmp1_1_eq), .GTin(cmp1_1_gt), .LT(cmp1_2_lt), .GT(cmp1_2_gt),
    .EQ(cmp1_2_eq));
  cmp1 cmp1_3 (
    .LTin(cmp1_2_lt), .A(A[1]), .B(B[1]), .EQin(cmp1_2_eq), .GTin(cmp1_2_gt), .LT(cmp1_3_lt), .GT(cmp1_3_gt),
    .EQ(cmp1_3_eq));
  cmp1 cmp1_4 (.LTin(cmp1_3_lt), .A(A[0]), .B(B[0]), .EQin(cmp1_3_eq), .GTin(cmp1_3_gt), .LT(LT), .GT(GT), .EQ(EQ));

  // Notes on the sheet:
  //   Group 38 | Roll number: CS25B035
endmodule

module cmp16 (
  input  [15:0] A,
  input  [15:0] B,
  output LT,
  output GT,
  output EQ
);

  wire cmp4_1_eq, cmp4_1_gt, cmp4_1_lt, cmp4_2_eq, cmp4_2_gt, cmp4_2_lt, cmp4_3_eq, cmp4_3_gt, cmp4_3_lt;
  wire [3:0] xor_1_out, xor_1_out_3, xor_2_out, xor_2_out_2, xor_2_out_3, xor_2_out_4;
  wire [15:4] xor_1_out_2;

  cmp4 cmp4_1 (
    .LTin(1'b0), .EQin(1'b1), .GTin(1'b0), .A(xor_1_out_2[15:12]), .B(xor_2_out_4), .LT(cmp4_1_lt),
    .GT(cmp4_1_gt), .EQ(cmp4_1_eq));
  assign {xor_1_out_2[15:12], xor_1_out_3, xor_1_out_2[7:4], xor_1_out} = A ^ 16'h8000;  // XOR_Gate xor_1, 16 bits wide
  cmp4 cmp4_2 (
    .LTin(cmp4_1_lt), .EQin(cmp4_1_eq), .GTin(cmp4_1_gt), .A(xor_1_out_3), .B(xor_2_out_3), .LT(cmp4_2_lt),
    .GT(cmp4_2_gt), .EQ(cmp4_2_eq));
  assign {xor_2_out_4, xor_2_out_3, xor_2_out_2, xor_2_out} = B ^ 16'h8000;  // XOR_Gate xor_2, 16 bits wide
  cmp4 cmp4_3 (
    .LTin(cmp4_2_lt), .EQin(cmp4_2_eq), .GTin(cmp4_2_gt), .A(xor_1_out_2[7:4]), .B(xor_2_out_2),
    .LT(cmp4_3_lt), .GT(cmp4_3_gt), .EQ(cmp4_3_eq));
  cmp4 cmp4_4 (
    .LTin(cmp4_3_lt), .EQin(cmp4_3_eq), .GTin(cmp4_3_gt), .A(xor_1_out), .B(xor_2_out), .LT(LT), .GT(GT),
    .EQ(EQ));

  // Notes on the sheet:
  //   Group 38 | Roll number: CS25B035
endmodule

module shiftLby1 (
  input  in_1,
  input  S0,
  input  [15:0] A,
  output [15:0] B
);

  Multiplexer multiplexer_1 (.in0(A[0]), .in1(in_1), .out(B[0]), .sel(S0));
  Multiplexer multiplexer_2 (.in0(A[1]), .in1(A[0]), .out(B[1]), .sel(S0));
  Multiplexer multiplexer_3 (.in0(A[2]), .in1(A[1]), .out(B[2]), .sel(S0));
  Multiplexer multiplexer_4 (.in0(A[3]), .in1(A[2]), .out(B[3]), .sel(S0));
  Multiplexer multiplexer_5 (.in0(A[4]), .in1(A[3]), .out(B[4]), .sel(S0));
  Multiplexer multiplexer_6 (.in0(A[5]), .in1(A[4]), .out(B[5]), .sel(S0));
  Multiplexer multiplexer_7 (.in0(A[6]), .in1(A[5]), .out(B[6]), .sel(S0));
  Multiplexer multiplexer_8 (.in0(A[7]), .in1(A[6]), .out(B[7]), .sel(S0));
  Multiplexer multiplexer_9 (.in0(A[8]), .in1(A[7]), .out(B[8]), .sel(S0));
  Multiplexer multiplexer_10 (.in0(A[9]), .in1(A[8]), .out(B[9]), .sel(S0));
  Multiplexer multiplexer_11 (.in0(A[10]), .in1(A[9]), .out(B[10]), .sel(S0));
  Multiplexer multiplexer_12 (.in0(A[11]), .in1(A[10]), .out(B[11]), .sel(S0));
  Multiplexer multiplexer_13 (.in0(A[12]), .in1(A[11]), .out(B[12]), .sel(S0));
  Multiplexer multiplexer_14 (.in0(A[13]), .in1(A[12]), .out(B[13]), .sel(S0));
  Multiplexer multiplexer_15 (.in0(A[14]), .in1(A[13]), .out(B[14]), .sel(S0));
  Multiplexer multiplexer_16 (.in0(A[15]), .in1(A[14]), .out(B[15]), .sel(S0));

  // Notes on the sheet:
  //   Group 38 | Roll number: CS25B035
endmodule

module shiftLby2 (
  input  in_1,
  input  [15:0] B,
  input  S1,
  output [15:0] C
);

  wire [15:0] shiftlby1_1_b;

  shiftLby1 shiftlby1_1 (.in_1(in_1), .S0(S1), .A(B), .B(shiftlby1_1_b));
  shiftLby1 shiftlby1_2 (.in_1(in_1), .S0(S1), .A(shiftlby1_1_b), .B(C));

  // Notes on the sheet:
  //   Group 38 | Roll number: CS25B035
endmodule

module shiftLby4 (
  input  in_1,
  input  [15:0] C,
  input  S2,
  output [15:0] D
);

  wire [15:0] shiftlby2_1_c;

  shiftLby2 shiftlby2_1 (.in_1(in_1), .B(C), .S1(S2), .C(shiftlby2_1_c));
  shiftLby2 shiftlby2_2 (.in_1(in_1), .B(shiftlby2_1_c), .S1(S2), .C(D));

  // Notes on the sheet:
  //   Group 38 | Roll number: CS25B035
endmodule

module shiftLby8 (
  input  in_1,
  input  [15:0] D,
  input  S3,
  output [15:0] E
);

  wire [15:0] shiftlby4_1_d;

  shiftLby4 shiftlby4_1 (.in_1(in_1), .C(D), .S2(S3), .D(shiftlby4_1_d));
  shiftLby4 shiftlby4_2 (.in_1(in_1), .C(shiftlby4_1_d), .S2(S3), .D(E));

  // Notes on the sheet:
  //   Group 38 | Roll number: CS25B035
endmodule

module shiftLby16 (
  input  [15:0] E,
  input  [15:0] in_2,
  input  S4,
  output [15:0] F
);

  Multiplexer #(.width(16)) multiplexer_1 (.in0(E), .in1(in_2), .out(F), .sel(S4));

  // Notes on the sheet:
  //   Group 38 | Roll number: CS25B035
endmodule

module SHL16 (
  input  [15:0] A,
  input  [4:0] SH,
  output [15:0] Y
);

  wire [15:0] shiftlby1_1_b, shiftlby2_1_c, shiftlby4_1_d, shiftlby8_1_e;

  shiftLby1 shiftlby1_1 (.in_1(1'b0), .S0(SH[0]), .A(A), .B(shiftlby1_1_b));
  shiftLby2 shiftlby2_1 (.in_1(1'b0), .B(shiftlby1_1_b), .S1(SH[1]), .C(shiftlby2_1_c));
  shiftLby4 shiftlby4_1 (.in_1(1'b0), .C(shiftlby2_1_c), .S2(SH[2]), .D(shiftlby4_1_d));
  shiftLby8 shiftlby8_1 (.in_1(1'b0), .D(shiftlby4_1_d), .S3(SH[3]), .E(shiftlby8_1_e));
  shiftLby16 shiftlby16_1 (.E(shiftlby8_1_e), .in_2({16{1'b0}}), .S4(SH[4]), .F(Y));

  // Notes on the sheet:
  //   Group 38 | Roll number: CS25B035
endmodule

module shiftRby1 (
  input  S0,
  input  [15:0] A,
  input  in_3,
  output [15:0] B
);

  Multiplexer multiplexer_1 (.in0(A[0]), .in1(A[1]), .out(B[0]), .sel(S0));
  Multiplexer multiplexer_2 (.in0(A[1]), .in1(A[2]), .out(B[1]), .sel(S0));
  Multiplexer multiplexer_3 (.in0(A[2]), .in1(A[3]), .out(B[2]), .sel(S0));
  Multiplexer multiplexer_4 (.in0(A[3]), .in1(A[4]), .out(B[3]), .sel(S0));
  Multiplexer multiplexer_5 (.in0(A[4]), .in1(A[5]), .out(B[4]), .sel(S0));
  Multiplexer multiplexer_6 (.in0(A[5]), .in1(A[6]), .out(B[5]), .sel(S0));
  Multiplexer multiplexer_7 (.in0(A[6]), .in1(A[7]), .out(B[6]), .sel(S0));
  Multiplexer multiplexer_8 (.in0(A[7]), .in1(A[8]), .out(B[7]), .sel(S0));
  Multiplexer multiplexer_9 (.in0(A[8]), .in1(A[9]), .out(B[8]), .sel(S0));
  Multiplexer multiplexer_10 (.in0(A[9]), .in1(A[10]), .out(B[9]), .sel(S0));
  Multiplexer multiplexer_11 (.in0(A[10]), .in1(A[11]), .out(B[10]), .sel(S0));
  Multiplexer multiplexer_12 (.in0(A[11]), .in1(A[12]), .out(B[11]), .sel(S0));
  Multiplexer multiplexer_13 (.in0(A[12]), .in1(A[13]), .out(B[12]), .sel(S0));
  Multiplexer multiplexer_14 (.in0(A[13]), .in1(A[14]), .out(B[13]), .sel(S0));
  Multiplexer multiplexer_15 (.in0(A[14]), .in1(A[15]), .out(B[14]), .sel(S0));
  Multiplexer multiplexer_16 (.in0(A[15]), .in1(in_3), .out(B[15]), .sel(S0));

  // Notes on the sheet:
  //   Group 38 | Roll number: CS25B035
endmodule

module shiftRby2 (
  input  S1,
  input  [15:0] B,
  input  in_3,
  output [15:0] C
);

  wire [15:0] shiftrby1_1_b;

  shiftRby1 shiftrby1_1 (.S0(S1), .A(B), .in_3(in_3), .B(shiftrby1_1_b));
  shiftRby1 shiftrby1_2 (.S0(S1), .A(shiftrby1_1_b), .in_3(in_3), .B(C));

  // Notes on the sheet:
  //   Group 38 | Roll number: CS25B035
endmodule

module shiftRby4 (
  input  S2,
  input  [15:0] C,
  input  in_3,
  output [15:0] D
);

  wire [15:0] shiftrby2_1_c;

  shiftRby2 shiftrby2_1 (.S1(S2), .B(C), .in_3(in_3), .C(shiftrby2_1_c));
  shiftRby2 shiftrby2_2 (.S1(S2), .B(shiftrby2_1_c), .in_3(in_3), .C(D));

  // Notes on the sheet:
  //   Group 38 | Roll number: CS25B035
endmodule

module shiftRby8 (
  input  S3,
  input  [15:0] D,
  input  in_3,
  output [15:0] E
);

  wire [15:0] shiftrby4_1_d;

  shiftRby4 shiftrby4_1 (.S2(S3), .C(D), .in_3(in_3), .D(shiftrby4_1_d));
  shiftRby4 shiftrby4_2 (.S2(S3), .C(shiftrby4_1_d), .in_3(in_3), .D(E));

  // Notes on the sheet:
  //   Group 38 | Roll number: CS25B035
endmodule

module shiftRby16 (
  input  S4,
  input  [15:0] E,
  input  in_3,
  output [15:0] F
);

  wire [15:0] shiftrby8_1_e;

  shiftRby8 shiftrby8_1 (.S3(S4), .D(E), .in_3(in_3), .E(shiftrby8_1_e));
  shiftRby8 shiftrby8_2 (.S3(S4), .D(shiftrby8_1_e), .in_3(in_3), .E(F));

  // Notes on the sheet:
  //   Group 38 | Roll number: CS25B035
endmodule

module SHR16 (
  input  [15:0] A,
  input  [4:0] SH,
  output [15:0] Y
);

  wire [15:0] shiftrby1_1_b, shiftrby2_1_c, shiftrby4_1_d, shiftrby8_1_e;

  shiftRby1 shiftrby1_1 (.S0(SH[0]), .A(A), .in_3(1'b0), .B(shiftrby1_1_b));
  shiftRby2 shiftrby2_1 (.S1(SH[1]), .B(shiftrby1_1_b), .in_3(1'b0), .C(shiftrby2_1_c));
  shiftRby4 shiftrby4_1 (.S2(SH[2]), .C(shiftrby2_1_c), .in_3(1'b0), .D(shiftrby4_1_d));
  shiftRby8 shiftrby8_1 (.S3(SH[3]), .D(shiftrby4_1_d), .in_3(1'b0), .E(shiftrby8_1_e));
  shiftRby16 shiftrby16_1 (.S4(SH[4]), .E(shiftrby8_1_e), .in_3(1'b0), .F(Y));

  // Notes on the sheet:
  //   Group 38 | Roll number: CS25B035
endmodule

module conditional_logic (
  input  [15:0] RESULT_INTERNAL,
  input  COUT,
  input  OVF,
  output ZERO,
  output NEGATIVE,
  output CARRY,
  output OVERFLOW
);

  wire or_1_out;

  or or_1 (or_1_out, RESULT_INTERNAL[0], RESULT_INTERNAL[1], RESULT_INTERNAL[2], RESULT_INTERNAL[3], RESULT_INTERNAL[4], RESULT_INTERNAL[5], RESULT_INTERNAL[6], RESULT_INTERNAL[7], RESULT_INTERNAL[8], RESULT_INTERNAL[9], RESULT_INTERNAL[10], RESULT_INTERNAL[11], RESULT_INTERNAL[12], RESULT_INTERNAL[13], RESULT_INTERNAL[14], RESULT_INTERNAL[15]);
  not not_1 (ZERO, or_1_out);

  assign CARRY = COUT;
  assign NEGATIVE = RESULT_INTERNAL[15];
  assign OVERFLOW = OVF;

  // Notes on the sheet:
  //   Group 38 | Roll number: CS25B035
endmodule

module Tri_state_buffer (
  input  [15:0] RESULT_INTERNAL,
  input  ALU_OUTPUT_ENABLE,
  output [15:0] BUS_OUT
);

  assign BUS_OUT = ALU_OUTPUT_ENABLE ? RESULT_INTERNAL : 16'bz;  // Controlled_Buffer controlled_buffer_1

  // Notes on the sheet:
  //   Group 38 | Roll number: CS25B035
endmodule

module ALU (
  input  [15:0] A,
  input  [15:0] B,
  input  ALU_OUTPUT_ENABLE,
  input  [4:0] OPCODE,
  output ZERO,
  output NEGATIVE,
  output CARRY,
  output OVERFLOW,
  output [15:0] BUS_OUT
);

  wire addsub16_1_cout, addsub16_1_ovf, cmp16_2_eq;
  wire [0:0] cmp16_1_lt;
  wire [15:0] addsub16_1_sum, and_1_out, mux_tree_1_result_internal, not_1_out, or_1_out, shl16_1_y,
       shr16_1_y, xor_1_out;

  assign and_1_out = A & B;  // AND_Gate and_1, 16 bits wide
  assign or_1_out = A | B;  // OR_Gate or_1, 16 bits wide
  assign xor_1_out = A ^ B;  // XOR_Gate xor_1, 16 bits wide
  assign not_1_out = ~A;  // NOT_Gate not_1, 16 bits wide
  addsub16 addsub16_1 (
    .A(A), .B(B), .SUB(cmp16_2_eq), .SUM(addsub16_1_sum), .OVF(addsub16_1_ovf), .COUT(addsub16_1_cout));
  cmp16 cmp16_1 (.A(A), .B(B), .LT(cmp16_1_lt[0]));  // open: GT, EQ
  SHL16 shl16_1 (.A(A), .SH(B[4:0]), .Y(shl16_1_y));
  SHR16 shr16_1 (.A(A), .SH(B[4:0]), .Y(shr16_1_y));
  mux_tree mux_tree_1 (
    .OPCODE(OPCODE), .ADD(addsub16_1_sum), .SUB(addsub16_1_sum), .AND16(and_1_out), .OR16(or_1_out),
    .XOR16(xor_1_out), .NOT16(not_1_out), .SHL(shl16_1_y), .SHR(shr16_1_y),
    .SLT({{15{1'b0}}, cmp16_1_lt[0]}), .RESULT_INTERNAL(mux_tree_1_result_internal));
  conditional_logic conditional_logic_1 (
    .RESULT_INTERNAL(mux_tree_1_result_internal), .COUT(addsub16_1_cout), .OVF(addsub16_1_ovf), .ZERO(ZERO),
    .NEGATIVE(NEGATIVE), .CARRY(CARRY), .OVERFLOW(OVERFLOW));
  cmp16 cmp16_2 (.A({{11{1'b0}}, OPCODE}), .B(16'ha), .EQ(cmp16_2_eq));  // open: LT, GT
  Tri_state_buffer tri_state_buffer_1 (
    .RESULT_INTERNAL(mux_tree_1_result_internal), .ALU_OUTPUT_ENABLE(ALU_OUTPUT_ENABLE), .BUS_OUT(BUS_OUT));

  // Notes on the sheet:
  //   Group 38 | Roll number: CS25B035
endmodule

module mux_tree (
  input  [4:0] OPCODE,
  input  [15:0] ADD,
  input  [15:0] SUB,
  input  [15:0] AND16,
  input  [15:0] OR16,
  input  [15:0] XOR16,
  input  [15:0] NOT16,
  input  [15:0] SHL,
  input  [15:0] SHR,
  input  [15:0] SLT,
  output [15:0] RESULT_INTERNAL
);

  wire [15:0] multiplexer_1_out, multiplexer_2_out, multiplexer_3_out, multiplexer_4_out, multiplexer_5_out,
       multiplexer_6_out, multiplexer_7_out, multiplexer_8_out, multiplexer_9_out, multiplexer_10_out,
       multiplexer_11_out, multiplexer_12_out, multiplexer_13_out, multiplexer_14_out, multiplexer_15_out,
       multiplexer_16_out, multiplexer_17_out, multiplexer_18_out, multiplexer_19_out, multiplexer_20_out,
       multiplexer_21_out, multiplexer_22_out, multiplexer_23_out, multiplexer_24_out, multiplexer_25_out,
       multiplexer_26_out, multiplexer_27_out, multiplexer_28_out, multiplexer_29_out, multiplexer_30_out;

  Multiplexer #(.width(16)) multiplexer_1 (
    .in0({16{1'b0}}), .in1({16{1'b0}}), .out(multiplexer_1_out), .sel(OPCODE[0]));
  Multiplexer #(.width(16)) multiplexer_2 (
    .in0({16{1'b0}}), .in1({16{1'b0}}), .out(multiplexer_2_out), .sel(OPCODE[0]));
  Multiplexer #(.width(16)) multiplexer_3 (
    .in0({16{1'b0}}), .in1({16{1'b0}}), .out(multiplexer_3_out), .sel(OPCODE[0]));
  Multiplexer #(.width(16)) multiplexer_4 (
    .in0({16{1'b0}}), .in1({16{1'b0}}), .out(multiplexer_4_out), .sel(OPCODE[0]));
  Multiplexer #(.width(16)) multiplexer_5 (.in0({16{1'b0}}), .in1(ADD), .out(multiplexer_5_out), .sel(OPCODE[0]));
  Multiplexer #(.width(16)) multiplexer_6 (.in0(SUB), .in1({16{1'b0}}), .out(multiplexer_6_out), .sel(OPCODE[0]));
  Multiplexer #(.width(16)) multiplexer_7 (.in0({16{1'b0}}), .in1(AND16), .out(multiplexer_7_out), .sel(OPCODE[0]));
  Multiplexer #(.width(16)) multiplexer_8 (.in0(OR16), .in1(XOR16), .out(multiplexer_8_out), .sel(OPCODE[0]));
  Multiplexer #(.width(16)) multiplexer_9 (.in0(NOT16), .in1(SHL), .out(multiplexer_9_out), .sel(OPCODE[0]));
  Multiplexer #(.width(16)) multiplexer_10 (.in0(SHR), .in1(SLT), .out(multiplexer_10_out), .sel(OPCODE[0]));
  Multiplexer #(.width(16)) multiplexer_11 (
    .in0({16{1'b0}}), .in1({16{1'b0}}), .out(multiplexer_11_out), .sel(OPCODE[0]));
  Multiplexer #(.width(16)) multiplexer_12 (
    .in0({16{1'b0}}), .in1({16{1'b0}}), .out(multiplexer_12_out), .sel(OPCODE[0]));
  Multiplexer #(.width(16)) multiplexer_13 (
    .in0({16{1'b0}}), .in1({16{1'b0}}), .out(multiplexer_13_out), .sel(OPCODE[0]));
  Multiplexer #(.width(16)) multiplexer_14 (
    .in0({16{1'b0}}), .in1({16{1'b0}}), .out(multiplexer_14_out), .sel(OPCODE[0]));
  Multiplexer #(.width(16)) multiplexer_15 (
    .in0({16{1'b0}}), .in1({16{1'b0}}), .out(multiplexer_15_out), .sel(OPCODE[0]));
  Multiplexer #(.width(16)) multiplexer_16 (
    .in0({16{1'b0}}), .in1({16{1'b0}}), .out(multiplexer_16_out), .sel(OPCODE[0]));
  Multiplexer #(.width(16)) multiplexer_17 (
    .in0(multiplexer_1_out), .in1(multiplexer_2_out), .out(multiplexer_17_out), .sel(OPCODE[1]));
  Multiplexer #(.width(16)) multiplexer_18 (
    .in0(multiplexer_3_out), .in1(multiplexer_4_out), .out(multiplexer_18_out), .sel(OPCODE[1]));
  Multiplexer #(.width(16)) multiplexer_19 (
    .in0(multiplexer_5_out), .in1(multiplexer_6_out), .out(multiplexer_19_out), .sel(OPCODE[1]));
  Multiplexer #(.width(16)) multiplexer_20 (
    .in0(multiplexer_7_out), .in1(multiplexer_8_out), .out(multiplexer_20_out), .sel(OPCODE[1]));
  Multiplexer #(.width(16)) multiplexer_21 (
    .in0(multiplexer_9_out), .in1(multiplexer_10_out), .out(multiplexer_21_out), .sel(OPCODE[1]));
  Multiplexer #(.width(16)) multiplexer_22 (
    .in0(multiplexer_11_out), .in1(multiplexer_12_out), .out(multiplexer_22_out), .sel(OPCODE[1]));
  Multiplexer #(.width(16)) multiplexer_23 (
    .in0(multiplexer_13_out), .in1(multiplexer_14_out), .out(multiplexer_23_out), .sel(OPCODE[1]));
  Multiplexer #(.width(16)) multiplexer_24 (
    .in0(multiplexer_15_out), .in1(multiplexer_16_out), .out(multiplexer_24_out), .sel(OPCODE[1]));
  Multiplexer #(.width(16)) multiplexer_25 (
    .in0(multiplexer_17_out), .in1(multiplexer_18_out), .out(multiplexer_25_out), .sel(OPCODE[2]));
  Multiplexer #(.width(16)) multiplexer_26 (
    .in0(multiplexer_19_out), .in1(multiplexer_20_out), .out(multiplexer_26_out), .sel(OPCODE[2]));
  Multiplexer #(.width(16)) multiplexer_27 (
    .in0(multiplexer_21_out), .in1(multiplexer_22_out), .out(multiplexer_27_out), .sel(OPCODE[2]));
  Multiplexer #(.width(16)) multiplexer_28 (
    .in0(multiplexer_23_out), .in1(multiplexer_24_out), .out(multiplexer_28_out), .sel(OPCODE[2]));
  Multiplexer #(.width(16)) multiplexer_29 (
    .in0(multiplexer_25_out), .in1(multiplexer_26_out), .out(multiplexer_29_out), .sel(OPCODE[3]));
  Multiplexer #(.width(16)) multiplexer_30 (
    .in0(multiplexer_27_out), .in1(multiplexer_28_out), .out(multiplexer_30_out), .sel(OPCODE[3]));
  Multiplexer #(.width(16)) multiplexer_31 (
    .in0(multiplexer_29_out), .in1(multiplexer_30_out), .out(RESULT_INTERNAL), .sel(OPCODE[4]));

  // Notes on the sheet:
  //   Group 38 | Roll number: CS25B035
endmodule

module dff (
  input  RST,
  input  D,
  input  CLK,
  input  EN,
  output Q
);

  wire multiplexer_1_out;

  Multiplexer multiplexer_1 (.in0(Q), .in1(D), .out(multiplexer_1_out), .sel(EN));
  D_Flip_Flop d_ff_1 (.D(multiplexer_1_out), .clk(CLK), .Q(Q), .reset(RST));  // open: Qn, preset

  // Notes on the sheet:
  //   Group 38 | Roll number: CS25B035
endmodule

module register16 (
  input  clk,
  input  en,
  input  rst,
  input  [15:0] d,
  output [15:0] q
);

  dff dff_1 (.RST(rst), .D(d[0]), .CLK(clk), .EN(en), .Q(q[0]));
  dff dff_2 (.RST(rst), .D(d[1]), .CLK(clk), .EN(en), .Q(q[1]));
  dff dff_3 (.RST(rst), .D(d[2]), .CLK(clk), .EN(en), .Q(q[2]));
  dff dff_4 (.RST(rst), .D(d[3]), .CLK(clk), .EN(en), .Q(q[3]));
  dff dff_5 (.RST(rst), .D(d[4]), .CLK(clk), .EN(en), .Q(q[4]));
  dff dff_6 (.RST(rst), .D(d[5]), .CLK(clk), .EN(en), .Q(q[5]));
  dff dff_7 (.RST(rst), .D(d[6]), .CLK(clk), .EN(en), .Q(q[6]));
  dff dff_8 (.RST(rst), .D(d[7]), .CLK(clk), .EN(en), .Q(q[7]));
  dff dff_9 (.RST(rst), .D(d[8]), .CLK(clk), .EN(en), .Q(q[8]));
  dff dff_10 (.RST(rst), .D(d[9]), .CLK(clk), .EN(en), .Q(q[9]));
  dff dff_11 (.RST(rst), .D(d[10]), .CLK(clk), .EN(en), .Q(q[10]));
  dff dff_12 (.RST(rst), .D(d[11]), .CLK(clk), .EN(en), .Q(q[11]));
  dff dff_13 (.RST(rst), .D(d[12]), .CLK(clk), .EN(en), .Q(q[12]));
  dff dff_14 (.RST(rst), .D(d[13]), .CLK(clk), .EN(en), .Q(q[13]));
  dff dff_15 (.RST(rst), .D(d[14]), .CLK(clk), .EN(en), .Q(q[14]));
  dff dff_16 (.RST(rst), .D(d[15]), .CLK(clk), .EN(en), .Q(q[15]));

  // Notes on the sheet:
  //   Group 38 | Roll number: CS25B035
endmodule

module regfile8x16 (
  input  rb_enb,
  input  rst,
  input  ra_enb,
  input  [2:0] ra,
  input  [2:0] rb,
  input  [15:0] din,
  input  we,
  input  [2:0] rd,
  input  clk,
  output [15:0] qa,
  output [15:0] qb
);

  wire decoder_1_out0, decoder_1_out1, decoder_1_out2, decoder_1_out3, decoder_1_out4, decoder_1_out5,
       decoder_1_out6, decoder_1_out7, decoder_2_out0, decoder_2_out1, decoder_2_out2, decoder_2_out3,
       decoder_2_out4, decoder_2_out5, decoder_2_out6, decoder_2_out7, decoder_3_out0, decoder_3_out1,
       decoder_3_out2, decoder_3_out3, decoder_3_out4, decoder_3_out5, decoder_3_out6, decoder_3_out7;
  wire [15:0] R0_q, R1_q, R2_q, R3_q, R4_q, R5_q, R6_q, R7_q;

  Decoder #(.select(3)) decoder_1 (
    .out0(decoder_1_out0), .out1(decoder_1_out1), .out2(decoder_1_out2), .out3(decoder_1_out3),
    .out4(decoder_1_out4), .out5(decoder_1_out5), .out6(decoder_1_out6), .out7(decoder_1_out7), .sel(rd),
    .en(we));
  Register #(.width(16)) R0 (.D(din), .en(decoder_1_out0), .clk(clk), .Q(R0_q), .clr(rst));
  Register #(.width(16)) R1 (.D(din), .en(decoder_1_out1), .clk(clk), .Q(R1_q), .clr(rst));
  Register #(.width(16)) R2 (.D(din), .en(decoder_1_out2), .clk(clk), .Q(R2_q), .clr(rst));
  Register #(.width(16)) R3 (.D(din), .en(decoder_1_out3), .clk(clk), .Q(R3_q), .clr(rst));
  Register #(.width(16)) R4 (.D(din), .en(decoder_1_out4), .clk(clk), .Q(R4_q), .clr(rst));
  Register #(.width(16)) R5 (.D(din), .en(decoder_1_out5), .clk(clk), .Q(R5_q), .clr(rst));
  Register #(.width(16)) R6 (.D(din), .en(decoder_1_out6), .clk(clk), .Q(R6_q), .clr(rst));
  Register #(.width(16)) R7 (.D(din), .en(decoder_1_out7), .clk(clk), .Q(R7_q), .clr(rst));
  Decoder #(.select(3)) decoder_2 (
    .out0(decoder_2_out0), .out1(decoder_2_out1), .out2(decoder_2_out2), .out3(decoder_2_out3),
    .out4(decoder_2_out4), .out5(decoder_2_out5), .out6(decoder_2_out6), .out7(decoder_2_out7), .sel(ra),
    .en(ra_enb));
  assign qa = decoder_2_out0 ? R0_q : 16'bz;  // Controlled_Buffer controlled_buffer_1
  assign qa = decoder_2_out1 ? R1_q : 16'bz;  // Controlled_Buffer controlled_buffer_2
  assign qa = decoder_2_out2 ? R2_q : 16'bz;  // Controlled_Buffer controlled_buffer_3
  assign qa = decoder_2_out3 ? R3_q : 16'bz;  // Controlled_Buffer controlled_buffer_4
  assign qa = decoder_2_out4 ? R4_q : 16'bz;  // Controlled_Buffer controlled_buffer_5
  assign qa = decoder_2_out5 ? R5_q : 16'bz;  // Controlled_Buffer controlled_buffer_6
  assign qa = decoder_2_out6 ? R6_q : 16'bz;  // Controlled_Buffer controlled_buffer_7
  assign qa = decoder_2_out7 ? R7_q : 16'bz;  // Controlled_Buffer controlled_buffer_8
  assign qb = decoder_3_out0 ? R0_q : 16'bz;  // Controlled_Buffer controlled_buffer_9
  assign qb = decoder_3_out1 ? R1_q : 16'bz;  // Controlled_Buffer controlled_buffer_10
  assign qb = decoder_3_out2 ? R2_q : 16'bz;  // Controlled_Buffer controlled_buffer_11
  assign qb = decoder_3_out3 ? R3_q : 16'bz;  // Controlled_Buffer controlled_buffer_12
  assign qb = decoder_3_out4 ? R4_q : 16'bz;  // Controlled_Buffer controlled_buffer_13
  assign qb = decoder_3_out5 ? R5_q : 16'bz;  // Controlled_Buffer controlled_buffer_14
  assign qb = decoder_3_out6 ? R6_q : 16'bz;  // Controlled_Buffer controlled_buffer_15
  assign qb = decoder_3_out7 ? R7_q : 16'bz;  // Controlled_Buffer controlled_buffer_16
  Decoder #(.select(3)) decoder_3 (
    .out0(decoder_3_out0), .out1(decoder_3_out1), .out2(decoder_3_out2), .out3(decoder_3_out3),
    .out4(decoder_3_out4), .out5(decoder_3_out5), .out6(decoder_3_out6), .out7(decoder_3_out7), .sel(rb),
    .en(rb_enb));

  // Notes on the sheet:
  //   Group 38 | Roll number: CS25B035
endmodule

module status_reg (
  input  RST,
  input  clk,
  input  status_we,
  input  Z_in,
  input  N_in,
  input  C_in,
  input  V_in,
  output Z,
  output N,
  output C,
  output V
);

  dff dff_1 (.RST(RST), .D(Z_in), .CLK(clk), .EN(status_we), .Q(Z));
  dff dff_2 (.RST(RST), .D(N_in), .CLK(clk), .EN(status_we), .Q(N));
  dff dff_3 (.RST(RST), .D(C_in), .CLK(clk), .EN(status_we), .Q(C));
  dff dff_4 (.RST(RST), .D(V_in), .CLK(clk), .EN(status_we), .Q(V));

  // Notes on the sheet:
  //   Group 38 | Roll number: CS25B035
endmodule

module ram_word (
  input  [15:0] addr,
  input  [15:0] din,
  input  mem_write,
  input  mem_read,
  input  clk,
  output [15:0] dout
);

  RAM #(.addrWidth(15), .asyncread("true")) ram_1 (
    .addr(addr[15:1]), .we(mem_write), .oe(mem_read), .clk(clk), .din(din[7:0]), .dout(dout[7:0]));
  RAM #(.addrWidth(15), .asyncread("true")) ram_2 (
    .addr(addr[15:1]), .we(mem_write), .oe(mem_read), .clk(clk), .din(din[15:8]), .dout(dout[15:8]));

  // Notes on the sheet:
  //   Group 38 | Roll number: CS25B035
endmodule

module PC_MAR_MDR_IR (
  input  CLK,
  input  RST,
  input  [15:0] MAR_D,
  input  MAR_EN,
  input  [15:0] MDR_D,
  input  MDR_EN,
  input  [15:0] IR_D,
  input  IR_EN,
  input  PC_LOAD,
  input  [15:0] PC_D,
  input  PC_EN,
  output [15:0] MAR_Q,
  output [15:0] MDR_Q,
  output [15:0] IR_Q,
  output [15:0] PC_Q
);

  wire [15:0] adder_1_out, multiplexer_1_out;

  Multiplexer #(.width(16)) multiplexer_1 (.in0(adder_1_out), .in1(PC_D), .out(multiplexer_1_out), .sel(PC_LOAD));
  register16 MAR (.clk(CLK), .en(MAR_EN), .rst(RST), .d(MAR_D), .q(MAR_Q));
  register16 MDR (.clk(CLK), .en(MDR_EN), .rst(RST), .d(MDR_D), .q(MDR_Q));
  register16 IR (.clk(CLK), .en(IR_EN), .rst(RST), .d(IR_D), .q(IR_Q));
  register16 PC (.clk(CLK), .en(PC_EN), .rst(RST), .d(multiplexer_1_out), .q(PC_Q));
  Adder #(.width(16)) adder_1 (.a(PC_Q), .b(16'h2), .out(adder_1_out));  // open: cin, cout

  // Notes on the sheet:
  //   Group 38 | Roll number: CS25B035
endmodule

module tara_datapath (
  input  [2:0] IMM_SEL,
  input  [1:0] RA_SEL,
  input  ALU_B_SEL,
  input  CLK,
  input  RST,
  input  status_we,
  input  ALU_A_SEL,
  input  MAR_LOAD,
  input  MDR_LOAD,
  input  [4:0] ALU_select,
  input  RF_WRITE,
  input  IR_LOAD,
  input  PC_LOAD,
  input  PC_EN,
  input  IR_OUT,
  input  RF_OUT,
  input  PC_OUT,
  input  MDR_OUT,
  input  ALU_OUT,
  input  IMM_OUT,
  input  RAM_OUT_LD,
  input  ACC_load,
  input  mem_write,
  input  mem_read,
  output Z,
  output N,
  output [15:0] PC,
  output [15:0] IR,
  output [4:0] opcode
);

  wire alu_1_carry, alu_1_negative, alu_1_overflow, alu_1_zero;
  wire [2:0] multiplexer_1_out, tara_decoder_1_ra, tara_decoder_1_rb, tara_decoder_1_rd;
  wire [4:0] tara_decoder_1_off5;
  wire [7:0] tara_decoder_1_imm8, tara_decoder_1_rel8;
  wire [10:0] tara_decoder_1_rel11;
  wire [15:0] controlled_buffer_1_out, imm_unit_1_imm, multiplexer_2_out, multiplexer_3_out,
       pc_mar_mdr_ir_1_mar_q, pc_mar_mdr_ir_1_mdr_q, ram_word_1_dout, regfile8x16_1_qa, regfile8x16_1_qb;

  PC_MAR_MDR_IR pc_mar_mdr_ir_1 (
    .CLK(CLK), .RST(RST), .MAR_D(controlled_buffer_1_out), .MAR_EN(MAR_LOAD),
    .MDR_D(controlled_buffer_1_out), .MDR_EN(MDR_LOAD), .IR_D(controlled_buffer_1_out), .IR_EN(IR_LOAD),
    .PC_LOAD(PC_LOAD), .PC_D(controlled_buffer_1_out), .PC_EN(PC_EN), .MAR_Q(pc_mar_mdr_ir_1_mar_q),
    .MDR_Q(pc_mar_mdr_ir_1_mdr_q), .IR_Q(IR), .PC_Q(PC));
  assign controlled_buffer_1_out = PC_OUT ? PC : 16'bz;  // Controlled_Buffer controlled_buffer_1
  assign controlled_buffer_1_out = IR_OUT ? IR : 16'bz;  // Controlled_Buffer controlled_buffer_2
  assign controlled_buffer_1_out = MDR_OUT ? pc_mar_mdr_ir_1_mdr_q : 16'bz;  // Controlled_Buffer controlled_buffer_3
  Multiplexer #(.select(2), .width(3)) multiplexer_1 (
    .in0(tara_decoder_1_ra), .in1(tara_decoder_1_rd), .in2(3'b110), .in3(3'b111), .out(multiplexer_1_out),
    .sel(RA_SEL));
  tara_decoder tara_decoder_1 (
    .IR(IR), .off5(tara_decoder_1_off5), .rel8(tara_decoder_1_rel8), .RB(tara_decoder_1_rb),
    .imm8(tara_decoder_1_imm8), .rel11(tara_decoder_1_rel11), .RA(tara_decoder_1_ra), .RD(tara_decoder_1_rd),
    .op(opcode));  // open: format
  assign controlled_buffer_1_out = IMM_OUT ? imm_unit_1_imm : 16'bz;  // Controlled_Buffer controlled_buffer_4
  assign controlled_buffer_1_out = RAM_OUT_LD ? ram_word_1_dout : 16'bz;  // Controlled_Buffer controlled_buffer_5
  ram_word ram_word_1 (
    .addr(pc_mar_mdr_ir_1_mar_q), .din(pc_mar_mdr_ir_1_mdr_q), .mem_write(mem_write), .mem_read(mem_read),
    .clk(CLK), .dout(ram_word_1_dout));
  imm_unit imm_unit_1 (
    .imm8(tara_decoder_1_imm8), .off5(tara_decoder_1_off5), .rel8(tara_decoder_1_rel8),
    .rel11(tara_decoder_1_rel11), .QA(regfile8x16_1_qa), .IMM_SEL(IMM_SEL), .IMM(imm_unit_1_imm));
  Multiplexer #(.width(16)) multiplexer_2 (
    .in0(regfile8x16_1_qb), .in1(imm_unit_1_imm), .out(multiplexer_2_out), .sel(ALU_B_SEL));
  regfile8x16 regfile8x16_1 (
    .rb_enb(1'b1), .rst(RST), .ra_enb(1'b1), .ra(multiplexer_1_out), .rb(tara_decoder_1_rb),
    .din(controlled_buffer_1_out), .we(RF_WRITE), .rd(tara_decoder_1_rd), .clk(CLK), .qa(regfile8x16_1_qa),
    .qb(regfile8x16_1_qb));
  assign controlled_buffer_1_out = RF_OUT ? regfile8x16_1_qa : 16'bz;  // Controlled_Buffer controlled_buffer_6
  Multiplexer #(.width(16)) multiplexer_3 (.in0(regfile8x16_1_qa), .in1(PC), .out(multiplexer_3_out), .sel(ALU_A_SEL));
  register16 ACC (.clk(CLK), .en(ACC_load), .rst(RST), .d(controlled_buffer_1_out));  // open: q
  ALU alu_1 (
    .A(multiplexer_3_out), .B(multiplexer_2_out), .ALU_OUTPUT_ENABLE(ALU_OUT), .OPCODE(ALU_select),
    .ZERO(alu_1_zero), .NEGATIVE(alu_1_negative), .CARRY(alu_1_carry), .OVERFLOW(alu_1_overflow),
    .BUS_OUT(controlled_buffer_1_out));
  status_reg status_reg_1 (
    .RST(RST), .clk(CLK), .status_we(status_we), .Z_in(alu_1_zero), .N_in(alu_1_negative),
    .C_in(alu_1_carry), .V_in(alu_1_overflow), .Z(Z), .N(N));  // open: C, V

  // Notes on the sheet:
  //   Group 38 | Roll number: CS25B035
endmodule

module imm_unit (
  input  [7:0] imm8,
  input  [4:0] off5,
  input  [7:0] rel8,
  input  [10:0] rel11,
  input  [15:0] QA,
  input  [2:0] IMM_SEL,
  output [15:0] IMM
);

  wire [14:0] R8S, R11S;
  wire [15:0] S5, S8, Z8;

  assign Z8 = {{8{1'b0}}, imm8};  // Bit_Extender bit_extender_1
  assign S8 = {{8{imm8[7]}}, imm8};  // Bit_Extender bit_extender_2
  assign S5 = {{11{off5[4]}}, off5};  // Bit_Extender bit_extender_3
  assign R8S = {{7{rel8[7]}}, rel8};  // Bit_Extender bit_extender_4
  assign R11S = {{4{rel11[10]}}, rel11};  // Bit_Extender bit_extender_5
  Multiplexer #(.select(3), .width(16)) multiplexer_1 (
    .in0(Z8), .in1(S8), .in2(S5), .in3({R8S, 1'b0}), .in4({R11S, 1'b0}), .in5(16'h2), .in6({imm8, QA[7:0]}),
    .in7({16{1'b0}}), .out(IMM), .sel(IMM_SEL));

  // Other names for the same wires on the sheet: LIHW[15:0] = {imm8, QA[7:0]}; QA_LO[7:0] = QA[7:0]; R8X2[15:1] = R8S;
  //   R11X2[15:1] = R11S

  // Notes on the sheet:
  //   imm_unit: every immediate / displacement form, chosen by IMM_SEL
  //   Group 38 | Roll number: CS25B035
endmodule

module control_unit (
  input  CLK,
  input  [4:0] opcode,
  input  N,
  input  RST,
  input  Z,
  output [3:0] T_STATE,
  output [31:0] cw,
  output HALT,
  output HALTED
);

  wire or_1_out;
  wire [3:0] adder_1_out, multiplexer_1_out;
  wire [31:0] rom_1_data;

  Adder #(.width(4)) adder_1 (.a(T_STATE), .b(4'b0001), .out(adder_1_out));  // open: cin, cout
  Multiplexer #(.width(4)) multiplexer_1 (.in0(adder_1_out), .in1(4'b0000), .out(multiplexer_1_out), .sel(cw[29]));
  ROM #(.addrWidth(11), .dataWidth(32)) rom_1 (.addr({Z, N, opcode, T_STATE}), .data(rom_1_data));
  Register #(.width(4)) register_1 (.D(multiplexer_1_out), .en(1'b1), .clk(CLK), .Q(T_STATE), .clr(RST));
  Multiplexer #(.width(32)) multiplexer_2 (.in0(rom_1_data), .in1({32{1'b0}}), .out(cw), .sel(HALTED));
  or or_1 (or_1_out, cw[30], HALTED);
  D_Flip_Flop d_ff_1 (.D(or_1_out), .clk(CLK), .Q(HALTED), .reset(RST));  // open: Qn, preset

  assign HALT = cw[30];

  // Notes on the sheet:
  //   Group 38 | Roll number: CS25B035
  //   contents of rom_1 (hex, n*v repeats v):
  //   81 5140 204 13*20000000 81 5140 204 60000000 12*20000000 81 5140 204 20000810 12*20000000 81 5140
  //   204 20000808 12*20000000 81 5140 204 2e000808 12*20000000 81 5140 204 60000000 12*20000000 81 5140
  //   204 60000000 12*20000000 81 5140 204 60000000 12*20000000 81 5140 204 60000000 12*20000000 81 5140
  //   204 20890c20 12*20000000 81 5140 204 208a0c20 12*20000000 81 5140 204 29c90c20 12*20000000 81 5140
  //   204 60000000 12*20000000 81 5140 204 208d0c20 12*20000000 81 5140 204 208e0c20 12*20000000 81 5140
  //   204 208f0c20 12*20000000 81 5140 204 20900c20 12*20000000 81 5140 204 28d10c20 12*20000000 81 5140
  //   204 28d20c20 12*20000000 81 5140 204 20930c20 12*20000000 81 5140 204 60000000 12*20000000 81 5140
  //   204 60000000 12*20000000 81 5140 204 60000000 12*20000000 81 5140 204 60000000 12*20000000 81 5140
  //   204 60000000 12*20000000 81 5140 204 60000000 12*20000000 81 5140 204 60000000 12*20000000 81 5140
  //   204 60000000 12*20000000 81 5140 204 60000000 12*20000000 81 5140 204 60000000 12*20000000 81 5140
  //   204 60000000 12*20000000 81 5140 204 60000000 12*20000000 81 5140 204 13*20000000 81 5140 204
  //   60000000 12*20000000 81 5140 204 20000810 12*20000000 81 5140 204 20000808 12*20000000 81 5140 204
  //   2e000808 12*20000000 81 5140 204 60000000 12*20000000 81 5140 204 60000000 12*20000000 81 5140 204
  //   60000000 12*20000000 81 5140 204 60000000 12*20000000 81 5140 204 20890c20 12*20000000 81 5140 204
  //   208a0c20 12*20000000 81 5140 204 29c90c20 12*20000000 81 5140 204 60000000 12*20000000 81 5140 204
  //   208d0c20 12*20000000 81 5140 204 208e0c20 12*20000000 81 5140 204 208f0c20 12*20000000 81 5140 204
  //   20900c20 12*20000000 81 5140 204 28d10c20 12*20000000 81 5140 204 28d20c20 12*20000000 81 5140 204
  //   20930c20 12*20000000 81 5140 204 60000000 12*20000000 81 5140 204 60000000 12*20000000 81 5140 204
  //   60000000 12*20000000 81 5140 204 60000000 12*20000000 81 5140 204 60000000 12*20000000 81 5140 204
  //   60000000 12*20000000 81 5140 204 60000000 12*20000000 81 5140 204 60000000 12*20000000 81 5140 204
  //   60000000 12*20000000 81 5140 204 60000000 12*20000000 81 5140 204 60000000 12*20000000 81 5140 204
  //   60000000 12*20000000 81 5140 204 13*20000000 81 5140 204 60000000 12*20000000 81 5140 204 20000810
  //   12*20000000 81 5140 204 20000808 12*20000000 81 5140 204 2e000808 12*20000000 81 5140 204 60000000
  //   12*20000000 81 5140 204 60000000 12*20000000 81 5140 204 60000000 12*20000000 81 5140 204 60000000
  //   12*20000000 81 5140 204 20890c20 12*20000000 81 5140 204 208a0c20 12*20000000 81 5140 204 29c90c20
  //   12*20000000 81 5140 204 60000000 12*20000000 81 5140 204 208d0c20 12*20000000 81 5140 204 208e0c20
  //   12*20000000 81 5140 204 208f0c20 12*20000000 81 5140 204 20900c20 12*20000000 81 5140 204 28d10c20
  //   12*20000000 81 5140 204 28d20c20 12*20000000 81 5140 204 20930c20 12*20000000 81 5140 204 60000000
  //   12*20000000 81 5140 204 60000000 12*20000000 81 5140 204 60000000 12*20000000 81 5140 204 60000000
  //   12*20000000 81 5140 204 60000000 12*20000000 81 5140 204 60000000 12*20000000 81 5140 204 60000000
  //   12*20000000 81 5140 204 60000000 12*20000000 81 5140 204 60000000 12*20000000 81 5140 204 60000000
  //   12*20000000 81 5140 204 60000000 12*20000000 81 5140 204 60000000 12*20000000 81 5140 204
  //   13*20000000 81 5140 204 60000000 12*20000000 81 5140 204 20000810 12*20000000 81 5140 204 20000808
  //   12*20000000 81 5140 204 2e000808 12*20000000 81 5140 204 60000000 12*20000000 81 5140 204 60000000
  //   12*20000000 81 5140 204 60000000 12*20000000 81 5140 204 60000000 12*20000000 81 5140 204 20890c20
  //   12*20000000 81 5140 204 208a0c20 12*20000000 81 5140 204 29c90c20 12*20000000 81 5140 204 60000000
  //   12*20000000 81 5140 204 208d0c20 12*20000000 81 5140 204 208e0c20 12*20000000 81 5140 204 208f0c20
  //   12*20000000 81 5140 204 20900c20 12*20000000 81 5140 204 28d10c20 12*20000000 81 5140 204 28d20c20
  //   12*20000000 81 5140 204 20930c20 12*20000000 81 5140 204 60000000 12*20000000 81 5140 204 60000000
  //   12*20000000 81 5140 204 60000000 12*20000000 81 5140 204 60000000 12*20000000 81 5140 204 60000000
  //   12*20000000 81 5140 204 60000000 12*20000000 81 5140 20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
endmodule

module tara_cpu (
  input  RST
);

  wire CLK_out, tara_datapath_1_n, tara_datapath_1_z;
  wire [4:0] tara_datapath_1_opcode;
  wire [31:0] control_unit_1_cw;

  Clock CLK (.out(CLK_out));
  control_unit control_unit_1 (
    .CLK(CLK_out), .opcode(tara_datapath_1_opcode), .N(tara_datapath_1_n), .RST(RST), .Z(tara_datapath_1_z),
    .cw(control_unit_1_cw));  // open: T_STATE, HALT, HALTED
  tara_datapath tara_datapath_1 (
    .IMM_SEL(control_unit_1_cw[26:24]), .RA_SEL(control_unit_1_cw[28:27]), .ALU_B_SEL(control_unit_1_cw[22]),
    .CLK(CLK_out), .RST(RST), .status_we(control_unit_1_cw[23]), .ALU_A_SEL(control_unit_1_cw[21]),
    .MAR_LOAD(control_unit_1_cw[7]), .MDR_LOAD(control_unit_1_cw[8]), .ALU_select(control_unit_1_cw[20:16]),
    .RF_WRITE(control_unit_1_cw[11]), .IR_LOAD(control_unit_1_cw[9]), .PC_LOAD(control_unit_1_cw[13]),
    .PC_EN(control_unit_1_cw[12]), .IR_OUT(control_unit_1_cw[1]), .RF_OUT(control_unit_1_cw[4]),
    .PC_OUT(control_unit_1_cw[0]), .MDR_OUT(control_unit_1_cw[2]), .ALU_OUT(control_unit_1_cw[5]),
    .IMM_OUT(control_unit_1_cw[3]), .RAM_OUT_LD(control_unit_1_cw[6]), .ACC_load(control_unit_1_cw[10]),
    .mem_write(control_unit_1_cw[15]), .mem_read(control_unit_1_cw[14]), .Z(tara_datapath_1_z),
    .N(tara_datapath_1_n), .opcode(tara_datapath_1_opcode));  // open: PC, IR

  // Notes on the sheet:
  //   Group 38 | Roll number: CS25B035
endmodule
